# Fritzing sketch Button (saved by Fritzing 0.9.3b)
breadboards: 1

parts:
  Max1 = chipKIT Max32 [chip_label=IC package="SIP (Single Inline) [THT]"]
  S1 = Pushbutton [package="[THT]"]
  R1 = Resistor [tolerance=±5% resistance=4.7k package="2512 [SMD]"]

nets:
  N1: Max1.3V3, R1.Pin_1
  N2: Max1.GND, S1.Pin_3, S1.Pin_4
  N3: Max1.D12, S1.Pin_1, S1.Pin_2, R1.Pin_0

custom parts:
  chipKIT Max32: chipKIT's Max32
